// Logisim project universal_register.circ as structural Verilog: 1 circuit, main circuit main
module main (
  input  Clear,
  input  S1,
  input  S2,
  input  SInright,
  input  SInleft,
  input  P4,
  input  P3,
  input  P2,
  input  P1,
  output out_10,
  output out_11,
  output out_12,
  output out_13
);

  wire clock_1_out, multiplexer_1_out, multiplexer_2_out, multiplexer_3_out, multiplexer_4_out;

  D_Flip_Flop d_ff_1 (.D(multiplexer_1_out), .clk(clock_1_out), .Q(out_10), .reset(Clear));  // open: Qn, preset
  Clock clock_1 (.out(clock_1_out));
  Multiplexer #(.select(2)) multiplexer_1 (
    .in0(out_10), .in1(SInright), .in2(out_11), .in3(P4), .out(multiplexer_1_out), .sel({S2, S1}));
  D_Flip_Flop d_ff_2 (.D(multiplexer_2_out), .clk(clock_1_out), .Q(out_11), .reset(Clear));  // open: Qn, preset
  Multiplexer #(.select(2)) multiplexer_2 (
    .in0(out_11), .in1(out_10), .in2(out_12), .in3(P3), .out(multiplexer_2_out), .sel({S2, S1}));
  D_Flip_Flop d_ff_3 (.D(multiplexer_3_out), .clk(clock_1_out), .Q(out_12), .reset(Clear));  // open: Qn, preset
  Multiplexer #(.select(2)) multiplexer_3 (
    .in0(out_12), .in1(out_11), .in2(out_13), .in3(P2), .out(multiplexer_3_out), .sel({S2, S1}));
  D_Flip_Flop d_ff_4 (.D(multiplexer_4_out), .clk(clock_1_out), .Q(out_13), .reset(Clear));  // open: Qn, preset
  Multiplexer #(.select(2)) multiplexer_4 (
    .in0(out_13), .in1(out_12), .in2(SInleft), .in3(P1), .out(multiplexer_4_out), .sel({S2, S1}));
endmodule
